# Fritzing sketch sample (saved by Fritzing 0.9.3b)
circuit board: 15.24cm x 10.16cm
breadboards: 1

parts:
  LED1 = smd LED [color="Red (633nm)" package="1206 [SMD]"]
  LED2 = smd LED [color="Red (633nm)" package="1206 [SMD]"]
  LED3 = smd LED [color="Red (633nm)" package="1206 [SMD]"]
  R2 = Resistor [tolerance=±5% resistance=220 package="0805 [SMD]"]
  R3 = Resistor [tolerance=±5% resistance=220 package="0805 [SMD]"]
  R4 = Resistor [tolerance=±5% resistance=220 package="0805 [SMD]"]
  Part1 = Arduino Uno (Rev3)

nets:
  N1: LED1.cathode, R2.Pin_0
  N2: LED1.anode, Part1.D5_PWM
  N3: LED2.cathode, R3.Pin_0
  N4: LED2.anode, Part1.D7
  N5: LED3.cathode, R4.Pin_0
  N6: LED3.anode, Part1.D6_PWM
  N7: R2.Pin_1, R3.Pin_1, R4.Pin_1, Part1.GND
